// Logisim project TallerLogica-Combinatorios.circ as structural Verilog: 13 circuits, main circuit sumador_simple
module sumador_simple (
  input  A,
  input  B,
  output S,
  output Cout
);

  and and_1 (Cout, A, B);
  xor xor_1 (S, A, B);
endmodule

module sumador_completo (
  input  Cin,
  input  A,
  input  B,
  output S,
  output Cout
);

  wire and_1_out, and_2_out, xor_1_out;

  xor xor_1 (xor_1_out, A, B);
  and and_1 (and_1_out, Cin, xor_1_out);
  and and_2 (and_2_out, A, B);
  xor xor_2 (S, Cin, xor_1_out);
  or or_1 (Cout, and_1_out, and_2_out);
endmodule

module sumador_4 (
  input  Cin,
  input  [3:0] A,
  input  [3:0] B,
  output [3:0] S,
  output Cout
);

  wire sumador_completo_1_cout, sumador_completo_2_cout, sumador_completo_3_cout;

  sumador_completo sumador_completo_1 (.Cin(Cin), .A(A[0]), .B(B[0]), .S(S[0]), .Cout(sumador_completo_1_cout));
  sumador_completo sumador_completo_2 (
    .Cin(sumador_completo_1_cout), .A(A[1]), .B(B[1]), .S(S[1]), .Cout(sumador_completo_2_cout));
  sumador_completo sumador_completo_3 (
    .Cin(sumador_completo_2_cout), .A(A[2]), .B(B[2]), .S(S[2]), .Cout(sumador_completo_3_cout));
  sumador_completo sumador_completo_4 (.Cin(sumador_completo_3_cout), .A(A[3]), .B(B[3]), .S(S[3]), .Cout(Cout));
  Hex_Digit_Display hex_digit_display_1 (.value(S));  // open: dp
endmodule

module comparador_cero (
  input  [3:0] A,
  output Z
);

  wire or_1_out, or_2_out, or_3_out;

  or or_1 (or_1_out, A[0], A[1]);
  or or_2 (or_2_out, or_1_out, A[2]);
  or or_3 (or_3_out, or_2_out, A[3]);
  not not_1 (Z, or_3_out);
endmodule

module sumador_flags (
  input  Cin,
  input  [3:0] A,
  input  [3:0] B,
  output [3:0] S,
  output N,
  output Z,
  output V,
  output C
);

  wire and_1_out, and_2_out, not_1_out, not_2_out, sumador_completo_1_cout, sumador_completo_2_cout,
       sumador_completo_2_s, sumador_completo_3_cout, xor_1_out;

  not not_1 (not_1_out, A[3]);
  not not_2 (not_2_out, B[3]);
  and and_1 (and_1_out, not_1_out, not_2_out);
  and and_2 (and_2_out, A[3], B[3]);
  xor xor_1 (xor_1_out, and_1_out, and_2_out);
  sumador_completo sumador_completo_1 (.A(A[0]), .B(B[0]), .Cout(sumador_completo_1_cout));  // open: Cin, S
  sumador_completo sumador_completo_2 (
    .Cin(sumador_completo_1_cout), .A(A[1]), .B(B[1]), .S(sumador_completo_2_s),
    .Cout(sumador_completo_2_cout));
  sumador_completo sumador_completo_3 (
    .Cin(sumador_completo_2_cout), .A(A[2]), .B(B[2]), .Cout(sumador_completo_3_cout));  // open: S
  sumador_4 sumador_4_1 (.Cin(Cin), .A(A), .B(B), .S({N, S[2:0]}), .Cout(C));
  and and_3 (V, xor_1_out, sumador_completo_3_cout);
  comparador_cero comparador_cero_1 (.A({N, S[2:0]}), .Z(Z));
  Hex_Digit_Display hex_digit_display_1 (.value({N, S[2:0]}));  // open: dp

  assign S[3] = N;

  // Notes on the sheet:
  //   aca habia un solo or
endmodule

module incrementador_4 (
  input  [3:0] A,
  output [3:0] S
);

  sumador_4 sumador_4_1 (.A(A), .B(4'b0001), .S(S));  // open: Cin, Cout
  Hex_Digit_Display hex_digit_display_1 (.value(S));  // open: dp
endmodule

module inversor_4 (
  input  [3:0] A,
  input  INV,
  output [3:0] S
);

  wire [3:0] incrementador_4_1_s, xor_1_out;

  xor xor_1 (xor_1_out[0], A[0], INV);
  xor xor_2 (xor_1_out[1], A[1], INV);
  xor xor_3 (xor_1_out[2], A[2], INV);
  xor xor_4 (xor_1_out[3], A[3], INV);
  incrementador_4 incrementador_4_1 (.A(xor_1_out), .S(incrementador_4_1_s));
  Multiplexer #(.width(4)) multiplexer_1 (.in0(A), .in1(incrementador_4_1_s), .out(S), .sel(INV));
  Hex_Digit_Display hex_digit_display_1 (.value(S));  // open: dp
endmodule

module ALU (
  input  [3:0] A,
  input  [3:0] B,
  input  [1:0] OP,
  output [3:0] S,
  output N,
  output Z,
  output V,
  output C
);

  wire andbab_1_n, comparador_cero_1_z, comparador_cero_2_z, orbab_1_n, sumador_flags_1_c, sumador_flags_1_n,
       sumador_flags_1_v, sumador_flags_1_z, sumador_flags_2_c, sumador_flags_2_n, sumador_flags_2_v,
       sumador_flags_2_z;
  wire [3:0] andbab_1_s, inversor_4_1_s, orbab_1_s, sumador_flags_1_s, sumador_flags_2_s;

  ORBAB orbab_1 (.A(A), .B(B), .S(orbab_1_s), .N(orbab_1_n));
  ANDBAB andbab_1 (.A(A), .B(B), .S(andbab_1_s), .N(andbab_1_n));
  inversor_4 inversor_4_1 (.A(B), .INV(1'b1), .S(inversor_4_1_s));
  sumador_flags sumador_flags_1 (
    .A(A), .B(B), .S(sumador_flags_1_s), .N(sumador_flags_1_n), .Z(sumador_flags_1_z), .V(sumador_flags_1_v),
    .C(sumador_flags_1_c));  // open: Cin
  sumador_flags sumador_flags_2 (
    .A(A), .B(inversor_4_1_s), .S(sumador_flags_2_s), .N(sumador_flags_2_n), .Z(sumador_flags_2_z),
    .V(sumador_flags_2_v), .C(sumador_flags_2_c));  // open: Cin
  comparador_cero comparador_cero_1 (.Z(comparador_cero_1_z));  // open: A
  comparador_cero comparador_cero_2 (.Z(comparador_cero_2_z));  // open: A
  Hex_Digit_Display hex_digit_display_1 (.value(S));  // open: dp
  Multiplexer #(.select(2), .width(4)) multiplexer_1 (
    .in0(sumador_flags_1_s), .in1(sumador_flags_2_s), .in2(andbab_1_s), .in3(orbab_1_s), .out(S), .sel(OP));
  Multiplexer #(.select(2)) multiplexer_2 (
    .in0(sumador_flags_1_n), .in1(sumador_flags_2_n), .in2(andbab_1_n), .in3(orbab_1_n), .out(N), .sel(OP));
  Multiplexer #(.select(2)) multiplexer_3 (
    .in0(sumador_flags_1_z), .in1(sumador_flags_2_z), .in2(comparador_cero_1_z), .in3(comparador_cero_2_z),
    .out(Z), .sel(OP));
  Multiplexer #(.select(2)) multiplexer_4 (
    .in0(sumador_flags_2_v), .in1(sumador_flags_1_v), .in2(1'b0), .in3(1'b0), .out(V), .sel(OP));
  Multiplexer #(.select(2)) multiplexer_5 (
    .in0(sumador_flags_2_c), .in1(sumador_flags_1_c), .in2(1'b0), .in3(1'b0), .out(C), .sel(OP));
endmodule

module verificador (
  output [3:0] out_1,
  output [3:0] out_2,
  output [1:0] out_3,
  output halt,
  output N,
  output Z,
  output V,
  output C,
  output [3:0] res
);

  wire clock_1_out;

  Clock clock_1 (.out(clock_1_out));
  Counter #(.max('h3ff), .width(10)) counter_1 (
    .clk(clock_1_out), .carry(halt), .Q({out_3, out_2, out_1}));  // open: clr, load, up, count, D
  // ALU alu_1: pin names not known; wires that end beside it: out_1, out_2, out_3, N, Z, V, C, res
endmodule

module ORBAB (
  input  [3:0] A,
  input  [3:0] B,
  output [3:0] S,
  output N
);

  or or_1 (S[0], A[0], B[0]);
  or or_2 (S[1], A[1], B[1]);
  or or_3 (S[2], A[2], B[2]);
  or or_4 (N, A[3], B[3]);

  assign S[3] = N;
endmodule

module ANDBAB (
  input  [3:0] A,
  input  [3:0] B,
  output [3:0] S,
  output N
);

  and and_1 (S[0], A[0], B[0]);
  and and_2 (S[1], A[1], B[1]);
  and and_3 (S[2], A[2], B[2]);
  and and_4 (N, A[3], B[3]);

  assign S[3] = N;
endmodule

module ALU2 (
  input  [1:0] OP,
  input  [3:0] A,
  input  [3:0] B,
  output [3:0] S,
  output Z,
  output C,
  output V,
  output N
);

  wire andbab_1_n, borrow_1_ee, borrow_2_ee, borrow_3_ee, borrow_4_ee, comparador_cero_1_z,
       comparador_cero_2_z, or_1_out, or_2_out, or_3_out, orbab_1_n, sumador_flags_1_c, sumador_flags_1_n,
       sumador_flags_1_v, sumador_flags_1_z, sumador_flags_2_n, sumador_flags_2_v, sumador_flags_2_z;
  wire [3:0] andbab_1_s, inversor_4_1_s, orbab_1_s, sumador_flags_1_s, sumador_flags_2_s;

  inversor_4 inversor_4_1 (.A(B), .INV(1'b1), .S(inversor_4_1_s));
  borrow borrow_1 (.A(A[0]), .B(B[0]), .EE(borrow_1_ee));
  borrow borrow_2 (.A(A[1]), .B(B[1]), .EE(borrow_2_ee));
  borrow borrow_3 (.A(A[2]), .B(B[2]), .EE(borrow_3_ee));
  borrow borrow_4 (.A(A[3]), .B(B[3]), .EE(borrow_4_ee));
  sumador_flags sumador_flags_1 (
    .A(A), .B(B), .S(sumador_flags_1_s), .N(sumador_flags_1_n), .Z(sumador_flags_1_z), .V(sumador_flags_1_v),
    .C(sumador_flags_1_c));  // open: Cin
  ANDBAB andbab_1 (.A(A), .B(B), .S(andbab_1_s), .N(andbab_1_n));
  ORBAB orbab_1 (.A(A), .B(B), .S(orbab_1_s), .N(orbab_1_n));
  or or_1 (or_1_out, borrow_1_ee, borrow_2_ee);
  or or_2 (or_2_out, borrow_3_ee, borrow_4_ee);
  sumador_flags sumador_flags_2 (
    .A(A), .B(inversor_4_1_s), .S(sumador_flags_2_s), .N(sumador_flags_2_n), .Z(sumador_flags_2_z),
    .V(sumador_flags_2_v));  // open: Cin, C
  or or_3 (or_3_out, or_1_out, or_2_out);
  comparador_cero comparador_cero_1 (.A(andbab_1_s), .Z(comparador_cero_1_z));
  comparador_cero comparador_cero_2 (.A(orbab_1_s), .Z(comparador_cero_2_z));
  Multiplexer #(.select(2)) multiplexer_1 (
    .in0(sumador_flags_1_c), .in1(or_3_out), .in2(1'b0), .in3(1'b0), .out(C), .sel(OP));
  Multiplexer #(.select(2)) multiplexer_2 (
    .in0(sumador_flags_1_z), .in1(sumador_flags_2_z), .in2(comparador_cero_1_z), .in3(comparador_cero_2_z),
    .out(Z), .sel(OP));
  Multiplexer #(.select(2)) multiplexer_3 (
    .in0(sumador_flags_1_v), .in1(sumador_flags_2_v), .in2(1'b0), .in3(1'b0), .out(V), .sel(OP));
  Multiplexer #(.select(2), .width(4)) multiplexer_4 (
    .in0(sumador_flags_1_s), .in1(sumador_flags_2_s), .in2(andbab_1_s), .in3(orbab_1_s), .out(S), .sel(OP));
  Multiplexer #(.select(2)) multiplexer_5 (
    .in0(sumador_flags_1_n), .in1(sumador_flags_2_n), .in2(andbab_1_n), .in3(orbab_1_n), .out(N), .sel(OP));
  Hex_Digit_Display hex_digit_display_1 (.value(S));  // open: dp

  // Notes on the sheet:
  //   V
  //   C
  //   N
  //   Z
endmodule

module borrow (
  input  A,
  input  B,
  output EE
);

  wire not_1_out;

  not not_1 (not_1_out, A);
  and and_1 (EE, not_1_out, B);
endmodule
